# Fritzing sketch Schematic (saved by Fritzing 0.9.2b)
breadboards: 1

parts:
  Part1 = Arduino Uno (Rev3)
  R1 = Resistor [tolerance=±5% resistance=220 package=THT]
  C2 = Electrolytic Capacitor [capacitance=1µF package="100 mil [THT, electrolytic]"]
  VCC1 = 4 x AAA Battery Mount

nets:
  N1: Part1.D9_PWM, R1.Pin_0
  N2: C2.+, VCC1.-, VCC1.+

notes:
  RGB LED Strip
  For more information on how to power RGB LED strip visit
  https://learn.adafruit.com/adafruit-neopixel-uberguide/power
